# Fritzing sketch ESP8266-PMS5003-DHT22 (saved by Fritzing 0.9.3b)
breadboards: 1

parts:
  U1 = NodeMCU V1.0
  DHT1 = DHT22 Humidity and Temperature Sensor
  R1 = Resistor [tolerance=±5% resistance=10k package="1206 [SMD]"]
  U3 = Hirose DF13 Series Header [part_number=PMS5003 package=DF13C-8P-1.25V]

nets:
  N1: U1.D0, U3.3
  N2: U1.D2, DHT1.DATA, R1.Pin_0
  GND: U1.GND, DHT1.GND, U3.2
  N3: U1.RX, U3.5
  VIN: U1.Vin, DHT1.VDD, R1.Pin_1, U3.1

custom parts:
  NodeMCU V1.0: ESP9266 based NodeMCU
